# Fritzing sketch ESP32-TEST (saved by Fritzing 0.9.3b)

parts:
  R1 = Resistor [tolerance=±5% resistance=220 package=THT]
  D1 = Rectifier Diode [part_number=1N4001 package="300 mil [THT]"]
  IC1 = ESP32-DevKitC [package="DIP (Dual Inline) [THT]"]

nets:
  N1: R1.Pin_0, IC1.pin38
  N2: R1.Pin_1, IC1.pin1
  N3: D1.cathode, IC1.pin29
  N4: D1.anode, IC1.pin37
